// Logisim project Eddy_kubwimana_lab4.circ as structural Verilog: 19 circuits, main circuit main
module main (
  input  I3,
  input  I2,
  input  I1,
  input  I0,
  input  Enable,
  input  reset,
  output Q3,
  output Q2,
  output Q1,
  output Q0
);

  wire clk_out, multiplexer_1_out, multiplexer_2_out, multiplexer_3_out, multiplexer_4_out;

  Multiplexer multiplexer_1 (.in0(Q3), .in1(I3), .out(multiplexer_1_out), .sel(Enable));
  D_Flip_Flop d_ff_1 (.D(multiplexer_1_out), .clk(clk_out), .Q(Q3), .reset(reset));  // open: Qn, preset
  Clock clk (.out(clk_out));
  Multiplexer multiplexer_2 (.in0(Q2), .in1(I2), .out(multiplexer_2_out), .sel(Enable));
  D_Flip_Flop d_ff_2 (.D(multiplexer_2_out), .clk(clk_out), .Q(Q2), .reset(reset));  // open: Qn, preset
  Multiplexer multiplexer_3 (.in0(Q1), .in1(I1), .out(multiplexer_3_out), .sel(Enable));
  D_Flip_Flop d_ff_3 (.D(multiplexer_3_out), .clk(clk_out), .Q(Q1), .reset(reset));  // open: Qn, preset
  Multiplexer multiplexer_4 (.in0(Q0), .in1(I0), .out(multiplexer_4_out), .sel(Enable));
  D_Flip_Flop d_ff_4 (.D(multiplexer_4_out), .clk(clk_out), .Q(Q0), .reset(reset));  // open: Qn, preset

  // Notes on the sheet:
  //   Implementing Register Enable
endmodule

module fullbitadder (
  input  A,
  input  B,
  input  cin,
  output sum,
  output Carry
);

  wire and_1_out, and_2_out, and_3_out, xor_1_out;

  xor xor_1 (xor_1_out, A, B);
  xor xor_2 (sum, xor_1_out, cin);
  and and_1 (and_1_out, A, B);
  and and_2 (and_2_out, B, cin);
  and and_3 (and_3_out, A, cin);
  or or_1 (Carry, and_1_out, and_2_out, and_3_out);

  // Notes on the sheet:
  //   Full adder
endmodule

module twofulladder (
  input  [1:0] A,
  input  Init_Cin,
  input  [1:0] B,
  output [1:0] sum1,
  output Final_Carry
);

  wire fullbitadder_1_carry;

  fullbitadder fullbitadder_1 (.A(A[0]), .B(B[0]), .cin(Init_Cin), .sum(sum1[0]), .Carry(fullbitadder_1_carry));
  fullbitadder fullbitadder_2 (.A(A[1]), .B(B[1]), .cin(fullbitadder_1_carry), .sum(sum1[1]), .Carry(Final_Carry));

  // Notes on the sheet:
  //   Two full adder
  //   A0+B0
  //   A1+B1
endmodule

module addsubtwobut (
  input  Controler,
  input  [1:0] A,
  input  [1:0] B,
  output [1:0] sum1,
  output Final_Carry
);

  wire fullbitadder_1_carry, xor_1_out, xor_2_out;

  xor xor_1 (xor_1_out, Controler, B[0]);
  xor xor_2 (xor_2_out, B[1], Controler);
  fullbitadder fullbitadder_1 (.A(A[0]), .B(xor_1_out), .cin(Controler), .sum(sum1[0]), .Carry(fullbitadder_1_carry));
  fullbitadder fullbitadder_2 (.A(A[1]), .B(xor_2_out), .cin(fullbitadder_1_carry), .sum(sum1[1]), .Carry(Final_Carry));

  // Notes on the sheet:
  //   A0+B0
  //   A1+B1
  //   ADD SUB TWO BIT ADDER
endmodule

module eightfulladder (
  input  [7:0] A,
  input  Controler,
  input  [7:0] B,
  output [7:0] Sum,
  output Carry
);

  wire twofulladder_1_final_carry, twofulladder_2_final_carry, twofulladder_3_final_carry;

  twofulladder twofulladder_1 (
    .A(A[1:0]), .Init_Cin(Controler), .B(B[1:0]), .sum1(Sum[1:0]), .Final_Carry(twofulladder_1_final_carry));
  twofulladder twofulladder_2 (
    .A(A[3:2]), .Init_Cin(twofulladder_1_final_carry), .B(B[3:2]), .sum1(Sum[3:2]),
    .Final_Carry(twofulladder_2_final_carry));
  twofulladder twofulladder_3 (
    .A(A[5:4]), .Init_Cin(twofulladder_2_final_carry), .B(B[5:4]), .sum1(Sum[5:4]),
    .Final_Carry(twofulladder_3_final_carry));
  twofulladder twofulladder_4 (
    .A(A[7:6]), .Init_Cin(twofulladder_3_final_carry), .B(B[7:6]), .sum1(Sum[7:6]), .Final_Carry(Carry));

  // Notes on the sheet:
  //   8full adder
endmodule

module eightfullsubadder (
  input  [7:0] A,
  input  Controller,
  input  [7:0] B,
  output [7:0] out_4,
  output out_5
);

  wire fullbitadder_1_carry, fullbitadder_2_carry, fullbitadder_3_carry, fullbitadder_4_carry,
       fullbitadder_5_carry, fullbitadder_6_carry, fullbitadder_7_carry, xor_1_out, xor_2_out, xor_3_out,
       xor_4_out, xor_5_out, xor_6_out, xor_7_out, xor_8_out;

  xor xor_1 (xor_1_out, Controller, B[0]);
  xor xor_2 (xor_2_out, Controller, B[1]);
  xor xor_3 (xor_3_out, Controller, B[2]);
  xor xor_4 (xor_4_out, Controller, B[3]);
  xor xor_5 (xor_5_out, Controller, B[4]);
  xor xor_6 (xor_6_out, Controller, B[5]);
  xor xor_7 (xor_7_out, Controller, B[6]);
  xor xor_8 (xor_8_out, Controller, B[7]);
  fullbitadder fullbitadder_1 (.A(A[0]), .B(xor_1_out), .cin(Controller), .sum(out_4[0]), .Carry(fullbitadder_1_carry));
  fullbitadder fullbitadder_2 (
    .A(A[1]), .B(xor_2_out), .cin(fullbitadder_1_carry), .sum(out_4[1]), .Carry(fullbitadder_2_carry));
  fullbitadder fullbitadder_3 (
    .A(A[2]), .B(xor_3_out), .cin(fullbitadder_2_carry), .sum(out_4[2]), .Carry(fullbitadder_3_carry));
  fullbitadder fullbitadder_4 (
    .A(A[3]), .B(xor_4_out), .cin(fullbitadder_3_carry), .sum(out_4[3]), .Carry(fullbitadder_4_carry));
  fullbitadder fullbitadder_5 (
    .A(A[4]), .B(xor_5_out), .cin(fullbitadder_4_carry), .sum(out_4[4]), .Carry(fullbitadder_5_carry));
  fullbitadder fullbitadder_6 (
    .A(A[5]), .B(xor_6_out), .cin(fullbitadder_5_carry), .sum(out_4[5]), .Carry(fullbitadder_6_carry));
  fullbitadder fullbitadder_7 (.A(A[6]), .B(xor_7_out), .sum(out_4[6]), .Carry(fullbitadder_7_carry));  // open: cin
  fullbitadder fullbitadder_8 (.A(A[7]), .B(xor_8_out), .cin(fullbitadder_7_carry), .sum(out_4[7]), .Carry(out_5));
endmodule

module twobitMultiplier (
  input  [1:0] A,
  input  [1:0] B,
  output [3:0] out_3
);

  wire and_2_out, and_3_out, and_4_out, fullbitadder_1_carry;

  and and_1 (out_3[0], A[0], B[0]);
  and and_2 (and_2_out, A[1], B[0]);
  and and_3 (and_3_out, A[0], B[1]);
  and and_4 (and_4_out, A[1], B[1]);
  fullbitadder fullbitadder_1 (
    .A(and_2_out), .B(and_3_out), .sum(out_3[1]), .Carry(fullbitadder_1_carry));  // open: cin
  fullbitadder fullbitadder_2 (.B(and_4_out), .cin(fullbitadder_1_carry), .sum(out_3[2]), .Carry(out_3[3]));  // open: A

  // Notes on the sheet:
  //   2-BIT MULTIPLIER
endmodule

module MemoryCell (
  input  WE,
  input  DIN,
  input  Clock,
  input  OE,
  input  Reset,
  output Dout,
  output storedData
);

  wire and_1_out, and_2_out, not_1_out, or_1_out;

  not not_1 (not_1_out, WE);
  and and_1 (and_1_out, storedData, not_1_out);
  and and_2 (and_2_out, WE, DIN);
  or or_1 (or_1_out, and_1_out, and_2_out);
  D_Flip_Flop d_ff_1 (.D(or_1_out), .clk(Clock), .Q(storedData), .reset(Reset));  // open: Qn, preset
  assign Dout = OE ? storedData : 1'bz;  // Controlled_Buffer controlled_buffer_1

  // Notes on the sheet:
  //   MEMORY CELL
endmodule

module threeBitMultiplier (
  input  [2:0] A,
  input  [2:0] B,
  output [5:0] Result
);

  wire and_2_out, and_3_out, and_4_out, and_5_out, and_6_out, and_7_out, and_8_out, and_9_out,
       fullbitadder_1_carry, fullbitadder_2_carry, fullbitadder_2_sum, fullbitadder_4_carry, undriven;

  and and_1 (Result[0], A[0], B[0]);
  and and_2 (and_2_out, A[1], B[0]);
  and and_3 (and_3_out, A[0], B[1]);
  and and_4 (and_4_out, A[2], B[0]);
  and and_5 (and_5_out, A[1], B[1]);
  and and_6 (and_6_out, A[0], B[2]);
  and and_7 (and_7_out, A[2], B[1]);
  and and_8 (and_8_out, A[1], B[2]);
  and and_9 (and_9_out, A[2], B[2]);
  fullbitadder fullbitadder_1 (
    .A(and_2_out), .B(and_3_out), .sum(Result[1]), .Carry(fullbitadder_1_carry));  // open: cin
  fullbitadder fullbitadder_2 (
    .A(and_4_out), .B(and_5_out), .cin(fullbitadder_1_carry), .sum(fullbitadder_2_sum),
    .Carry(fullbitadder_2_carry));
  fullbitadder fullbitadder_3 (.A(fullbitadder_2_sum), .B(and_6_out), .cin(undriven), .sum(Result[2]));  // open: Carry
  fullbitadder fullbitadder_4 (
    .A(and_7_out), .B(and_8_out), .cin(fullbitadder_2_carry), .sum(Result[3]), .Carry(fullbitadder_4_carry));
  fullbitadder fullbitadder_5 (
    .A(and_9_out), .cin(fullbitadder_4_carry), .sum(Result[4]), .Carry(Result[5]));  // open: B

  // Notes on the sheet:
  //   3BIT MULTIPLIER
endmodule

module eightbitaddsub (
  input  [7:0] A,
  input  controller,
  input  [7:0] B,
  output [7:0] out_4
);

  wire not_1_out, not_2_out;
  wire [7:0] adder_1_out, controlled_buffer_1_out, controlled_buffer_2_out, controlled_buffer_3_out,
       controlled_buffer_4_out, subtractor_1_out;

  assign controlled_buffer_1_out = not_1_out ? A : 8'bz;  // Controlled_Buffer controlled_buffer_1
  not not_1 (not_1_out, controller);
  assign controlled_buffer_2_out = not_2_out ? B : 8'bz;  // Controlled_Buffer controlled_buffer_2
  not not_2 (not_2_out, controller);
  assign controlled_buffer_3_out = controller ? A : 8'bz;  // Controlled_Buffer controlled_buffer_3
  assign controlled_buffer_4_out = controller ? B : 8'bz;  // Controlled_Buffer controlled_buffer_4
  Adder adder_1 (.a(controlled_buffer_1_out), .b(controlled_buffer_2_out), .out(adder_1_out));  // open: cin, cout
  Subtractor subtractor_1 (
    .a(controlled_buffer_3_out), .b(controlled_buffer_4_out), .out(subtractor_1_out));  // open: bin, bout
  Multiplexer #(.width(8)) multiplexer_1 (.in0(adder_1_out), .in1(subtractor_1_out), .out(out_4), .sel(controller));
endmodule

module eightBitAU (
  input  [7:0] A,
  input  Controller,
  input  [7:0] B,
  input  [1:0] Selector,
  output [7:0] result
);

  wire [7:0] divider_1_out, eightbitaddsub_1_out_4, multiplier_1_out;

  Multiplier multiplier_1 (.a(A), .b(B), .out(multiplier_1_out));  // open: cin, cout
  Divider divider_1 (.a(A), .b(B), .out(divider_1_out));  // open: upper, rem
  eightbitaddsub eightbitaddsub_1 (.A(A), .controller(Controller), .B(B), .out_4(eightbitaddsub_1_out_4));
  Multiplexer #(.select(2), .width(8)) multiplexer_1 (
    .in0(eightbitaddsub_1_out_4), .in1(multiplier_1_out), .in2(divider_1_out), .out(result), .sel(Selector));  // open: in3

  // Notes on the sheet:
  //   Arithmetic Unit
endmodule

module LU (
  input  [7:0] A,
  input  [7:0] B,
  output out_3,
  output out_4,
  output out_5
);

  Comparator comparator_1 (.a(A), .b(B), .gt(out_3), .eq(out_4), .lt(out_5));

  // Notes on the sheet:
  //   Logic Unit
endmodule

module ExtendedLu (
  input  [7:0] A,
  input  [7:0] B,
  input  [2:0] Selector,
  output Result
);

  wire comparator_1_eq, comparator_1_gt, comparator_1_lt, not_1_out, or_1_out, or_2_out;

  Comparator comparator_1 (.a(A), .b(B), .gt(comparator_1_gt), .eq(comparator_1_eq), .lt(comparator_1_lt));
  or or_1 (or_1_out, comparator_1_eq, comparator_1_gt);
  not not_1 (not_1_out, comparator_1_eq);
  or or_2 (or_2_out, comparator_1_eq, comparator_1_lt);
  Multiplexer #(.select(3)) multiplexer_1 (
    .in0(or_1_out), .in1(comparator_1_gt), .in2(comparator_1_eq), .in3(comparator_1_lt), .in4(or_2_out),
    .in5(not_1_out), .out(Result), .sel(Selector));  // open: in6, in7

  // Notes on the sheet:
  //   Extended LU
  //   COMPARATOR
  //   high or low
endmodule

module eightBitALU (
  input  Controller,
  input  [1:0] Selector,
  input  [7:0] A,
  input  [7:0] B,
  input  [2:0] LuSelector,
  input  OE,
  output [7:0] AU_DOUT,
  output [7:0] result,
  output high_low
);

  eightBitAU AU (.A(A), .Controller(Controller), .B(B), .Selector(Selector), .result(result));
  ExtendedLu LU (.A(A), .B(B), .Selector(LuSelector), .Result(high_low));
  assign AU_DOUT = OE ? result : 8'bz;  // Controlled_Buffer controlled_buffer_1

  // Notes on the sheet:
  //   8-BIT ALU
  //   0E
  //   AU DOUT
  //   8-bit result
  //   High and low
endmodule

module reg4bits (
  input  [3:0] DIN,
  input  WE,
  input  OE,
  input  RESET,
  input  CLOCK,
  output [3:0] DOUT,
  output [3:0] StoredData
);

  MemoryCell memorycell_1 (
    .WE(WE), .DIN(DIN[3]), .Clock(CLOCK), .OE(OE), .Reset(RESET), .Dout(DOUT[3]), .storedData(StoredData[3]));
  MemoryCell memorycell_2 (
    .WE(WE), .DIN(DIN[2]), .Clock(CLOCK), .OE(OE), .Reset(RESET), .Dout(DOUT[2]), .storedData(StoredData[2]));
  MemoryCell memorycell_3 (
    .WE(WE), .DIN(DIN[1]), .Clock(CLOCK), .OE(OE), .Reset(RESET), .Dout(DOUT[1]), .storedData(StoredData[1]));
  MemoryCell memorycell_4 (
    .WE(WE), .DIN(DIN[0]), .Clock(CLOCK), .OE(OE), .Reset(RESET), .Dout(DOUT[0]), .storedData(StoredData[0]));

  // Notes on the sheet:
  //   4 BITS REGISTER
endmodule

module reg8bits (
  input  [7:0] DIN,
  input  WE,
  input  OE,
  input  RESET,
  input  CLOCK,
  output [7:0] DOUT,
  output [7:0] StoredData
);

  reg4bits reg4bits_1 (
    .DIN(DIN[7:4]), .WE(WE), .OE(OE), .RESET(RESET), .CLOCK(CLOCK), .DOUT(DOUT[7:4]),
    .StoredData(StoredData[7:4]));
  reg4bits reg4bits_2 (
    .DIN(DIN[3:0]), .WE(WE), .OE(OE), .RESET(RESET), .CLOCK(CLOCK), .DOUT(DOUT[3:0]),
    .StoredData(StoredData[3:0]));

  // Notes on the sheet:
  //   8BIT REGISTER
endmodule

module ShiftRegister (
  input  SW,
  input  [5:0] PI_In,
  output Sout
);

  wire and_1_out, and_2_out, and_3_out, and_4_out, and_5_out, and_6_out, and_7_out, and_8_out, and_9_out,
       and_10_out, and_11_out, clk_out, d_ff_1_q, d_ff_2_q, d_ff_3_q, d_ff_4_q, d_ff_5_q, not_1_out,
       or_1_out, or_2_out, or_3_out, or_4_out, or_5_out;

  Clock clk (.out(clk_out));
  not not_1 (not_1_out, SW);
  D_Flip_Flop d_ff_1 (.D(and_1_out), .clk(clk_out), .Q(d_ff_1_q));  // open: Qn, preset, reset
  and and_1 (and_1_out, not_1_out, PI_In[0]);
  and and_2 (and_2_out, not_1_out, PI_In[1]);
  and and_3 (and_3_out, SW, d_ff_1_q);
  D_Flip_Flop d_ff_2 (.D(or_1_out), .clk(clk_out), .Q(d_ff_2_q));  // open: Qn, preset, reset
  or or_1 (or_1_out, and_2_out, and_3_out);
  and and_4 (and_4_out, not_1_out, PI_In[2]);
  and and_5 (and_5_out, d_ff_2_q, SW);
  D_Flip_Flop d_ff_3 (.D(or_2_out), .clk(clk_out), .Q(d_ff_3_q));  // open: Qn, preset, reset
  or or_2 (or_2_out, and_4_out, and_5_out);
  and and_6 (and_6_out, not_1_out, PI_In[3]);
  and and_7 (and_7_out, d_ff_3_q, SW);
  D_Flip_Flop d_ff_4 (.D(or_3_out), .clk(clk_out), .Q(d_ff_4_q));  // open: Qn, preset, reset
  or or_3 (or_3_out, and_6_out, and_7_out);
  and and_8 (and_8_out, not_1_out, PI_In[4]);
  and and_9 (and_9_out, d_ff_4_q, SW);
  D_Flip_Flop d_ff_5 (.D(or_4_out), .clk(clk_out), .Q(d_ff_5_q));  // open: Qn, preset, reset
  or or_4 (or_4_out, and_8_out, and_9_out);
  and and_10 (and_10_out, not_1_out, PI_In[5]);
  and and_11 (and_11_out, d_ff_5_q, SW);
  or or_5 (or_5_out, and_10_out, and_11_out);
  D_Flip_Flop d_ff_6 (.D(or_5_out), .clk(clk_out), .Q(Sout));  // open: Qn, preset, reset

  // Notes on the sheet:
  //   6bit parallel in / serial out register
endmodule

module Datapath (
  input  counter_oe,
  input  count_enable,
  input  WE_MAR,
  input  [7:0] test_data,
  input  OE_MAR,
  input  OE,
  input  in_7,
  input  in_8,
  input  in_9,
  input  WE0,
  input  OE_in,
  input  Reset_in,
  input  WE1,
  input  WE,
  input  Reset_A,
  input  OE_2,
  input  Controler,
  input  [1:0] ALU_SELECTOR,
  input  [2:0] LU_SELECT,
  input  OE_ALU,
  input  WE2,
  input  Reset_B,
  output [3:0] out_23,
  output [3:0] countrer_content,
  output [7:0] IR_content,
  output [7:0] MBR_CONT,
  output [7:0] REG_A_content,
  output [7:0] out_28,
  output [7:0] AU_RESULT,
  output LU_RESULT,
  output [7:0] REG_B_content
);

  wire clock_1_out;
  wire [3:0] controlled_buffer_1_out, decimaldecoder_2_dout, decimaldecoder_2_dout_2,
       decimaldecoder_2_dout_3, decimaldecoder_2_dout_5, decimaldecoder_2_dout_6, decimaldecoder_2_dout_7,
       decimaldecoder_3_dout_2, decimaldecoder_3_dout_3, decimaldecoder_3_dout_4, decimaldecoder_3_dout_5,
       MAR_dout;
  wire [7:0] bit_extender_1_out, eightbitalu_1_au_dout, Instruction_Register_dout;
  wire [15:0] decimaldecoder_3_dout;
  wire [15:12] decimaldecoder_3_dout_6;
  wire [31:0] decimaldecoder_1_dout, decimaldecoder_4_dout;
  wire [31:12] decimaldecoder_2_dout_4;

  _7_Segment_Display u_7_segment_display_1 (
    .g(decimaldecoder_1_dout[3]), .f(decimaldecoder_1_dout[2]), .a(decimaldecoder_1_dout[1]),
    .b(decimaldecoder_1_dout[0]), .e(decimaldecoder_1_dout[19]), .d(decimaldecoder_1_dout[18]),
    .c(decimaldecoder_1_dout[17]), .dp(decimaldecoder_1_dout[16]));
  DecimalDecoder decimaldecoder_1 (.Din(bit_extender_1_out), .Dout(decimaldecoder_1_dout));
  Clock clock_1 (.out(clock_1_out));
  Counter #(.max('hf), .width(4)) counter_1 (
    .count(count_enable), .clk(clock_1_out), .D(controlled_buffer_1_out), .Q(countrer_content));  // open: clr, load, up, carry
  assign bit_extender_1_out = {{4{countrer_content[3]}}, countrer_content};  // Bit_Extender bit_extender_1
  reg8bits Instruction_Register (
    .DIN(eightbitalu_1_au_dout), .WE(WE0), .OE(OE_in), .RESET(Reset_in), .CLOCK(clock_1_out),
    .DOUT(Instruction_Register_dout), .StoredData(IR_content));
  DecimalDecoder decimaldecoder_2 (
    .Din(REG_B_content),
    .Dout({decimaldecoder_2_dout_4[31:28], decimaldecoder_2_dout_7, decimaldecoder_2_dout_6, decimaldecoder_2_dout_5, decimaldecoder_2_dout_4[15:12], decimaldecoder_2_dout_3, decimaldecoder_2_dout_2, decimaldecoder_2_dout}));
  _7_Segment_Display u_7_segment_display_2 (
    .g(decimaldecoder_2_dout_4[15]), .f(decimaldecoder_2_dout_4[14]), .a(decimaldecoder_2_dout_4[13]),
    .b(decimaldecoder_2_dout_4[12]), .e(decimaldecoder_2_dout_4[31]), .d(decimaldecoder_2_dout_4[30]),
    .c(decimaldecoder_2_dout_4[29]), .dp(decimaldecoder_2_dout_4[28]));
  assign controlled_buffer_1_out = counter_oe ? countrer_content : 4'bz;  // Controlled_Buffer controlled_buffer_1
  _7_Segment_Display u_7_segment_display_3 (
    .g(decimaldecoder_3_dout_2[3]), .f(decimaldecoder_3_dout_2[2]), .a(decimaldecoder_3_dout_2[1]),
    .b(decimaldecoder_3_dout_2[0]), .e(decimaldecoder_3_dout_5[3]), .d(decimaldecoder_3_dout_5[2]),
    .c(decimaldecoder_3_dout_5[1]), .dp(decimaldecoder_3_dout_5[0]));
  _7_Segment_Display u_7_segment_display_4 (
    .g(decimaldecoder_3_dout[15]), .f(decimaldecoder_3_dout[14]), .a(decimaldecoder_3_dout[13]),
    .b(decimaldecoder_3_dout[12]), .e(decimaldecoder_3_dout_6[15]), .d(decimaldecoder_3_dout_6[14]),
    .c(decimaldecoder_3_dout_6[13]), .dp(decimaldecoder_3_dout_6[12]));
  _7_Segment_Display u_7_segment_display_5 (
    .g(decimaldecoder_2_dout_2[3]), .f(decimaldecoder_2_dout_2[2]), .a(decimaldecoder_2_dout_2[1]),
    .b(decimaldecoder_2_dout_2[0]), .e(decimaldecoder_2_dout_6[3]), .d(decimaldecoder_2_dout_6[2]),
    .c(decimaldecoder_2_dout_6[1]), .dp(decimaldecoder_2_dout_6[0]));
  _7_Segment_Display u_7_segment_display_6 (
    .g(decimaldecoder_2_dout_3[3]), .f(decimaldecoder_2_dout_3[2]), .a(decimaldecoder_2_dout_3[1]),
    .b(decimaldecoder_2_dout_3[0]), .e(decimaldecoder_2_dout_7[3]), .d(decimaldecoder_2_dout_7[2]),
    .c(decimaldecoder_2_dout_7[1]), .dp(decimaldecoder_2_dout_7[0]));
  BitSelector #(.group(4)) bitselector_1 (.in(Instruction_Register_dout), .out(controlled_buffer_1_out), .sel(1'b0));
  _7_Segment_Display u_7_segment_display_7 (
    .g(decimaldecoder_3_dout[7]), .f(decimaldecoder_3_dout[6]), .a(decimaldecoder_3_dout[5]),
    .b(decimaldecoder_3_dout[4]), .e(decimaldecoder_3_dout_4[3]), .d(decimaldecoder_3_dout_4[2]),
    .c(decimaldecoder_3_dout_4[1]), .dp(decimaldecoder_3_dout_4[0]));
  _7_Segment_Display u_7_segment_display_8 (
    .g(decimaldecoder_3_dout[3]), .f(decimaldecoder_3_dout[2]), .a(decimaldecoder_3_dout[1]),
    .b(decimaldecoder_3_dout[0]), .e(decimaldecoder_3_dout_3[3]), .d(decimaldecoder_3_dout_3[2]),
    .c(decimaldecoder_3_dout_3[1]), .dp(decimaldecoder_3_dout_3[0]));
  reg8bits A (
    .DIN(eightbitalu_1_au_dout), .WE(WE1), .RESET(Reset_A), .CLOCK(clock_1_out), .StoredData(REG_A_content));  // open: OE, DOUT
  eightBitALU eightbitalu_1 (
    .Controller(Controler), .Selector(ALU_SELECTOR), .A(REG_A_content), .B(REG_B_content),
    .LuSelector(LU_SELECT), .OE(OE_ALU), .AU_DOUT(eightbitalu_1_au_dout), .result(AU_RESULT),
    .high_low(LU_RESULT));
  reg8bits B (
    .DIN(eightbitalu_1_au_dout), .WE(WE2), .RESET(Reset_B), .CLOCK(clock_1_out), .StoredData(REG_B_content));  // open: OE, DOUT
  _7_Segment_Display u_7_segment_display_9 (
    .g(decimaldecoder_2_dout[3]), .f(decimaldecoder_2_dout[2]), .a(decimaldecoder_2_dout[1]),
    .b(decimaldecoder_2_dout[0]), .e(decimaldecoder_2_dout_5[3]), .d(decimaldecoder_2_dout_5[2]),
    .c(decimaldecoder_2_dout_5[1]), .dp(decimaldecoder_2_dout_5[0]));
  LED D7 ();  // open: in
  LED D6 ();  // open: in
  assign eightbitalu_1_au_dout = OE ? test_data : 8'bz;  // Controlled_Buffer controlled_buffer_2
  DecimalDecoder decimaldecoder_3 (
    .Din(REG_A_content),
    .Dout({decimaldecoder_3_dout_6, decimaldecoder_3_dout_5, decimaldecoder_3_dout_4, decimaldecoder_3_dout_3, decimaldecoder_3_dout[15:12], decimaldecoder_3_dout_2, decimaldecoder_3_dout[7:0]}));
  LED D5 ();  // open: in
  LED D4 ();  // open: in
  LED D3 (.in(eightbitalu_1_au_dout[3]));
  LED D2 ();  // open: in
  LED D1 ();  // open: in
  LED D0 ();  // open: in
  assign eightbitalu_1_au_dout = in_7 ? MBR_CONT : 8'bz;  // Controlled_Buffer controlled_buffer_3
  reg4bits MAR (
    .DIN(controlled_buffer_1_out), .WE(WE_MAR), .OE(OE_MAR), .CLOCK(clock_1_out), .DOUT(MAR_dout),
    .StoredData(out_23));  // open: RESET
  reg8bits MBR (
    .DIN(eightbitalu_1_au_dout), .WE(in_8), .OE(in_9), .CLOCK(clock_1_out), .DOUT(eightbitalu_1_au_dout),
    .StoredData(MBR_CONT));  // open: RESET
  reg8bits reg8bits_1 (
    .DIN(eightbitalu_1_au_dout), .WE(WE), .OE(OE_2), .CLOCK(clock_1_out), .DOUT(eightbitalu_1_au_dout),
    .StoredData(out_28));  // open: RESET
  DecimalDecoder decimaldecoder_4 (.Din(out_28), .Dout(decimaldecoder_4_dout));
  _7_Segment_Display u_7_segment_display_10 (
    .g(decimaldecoder_4_dout[15]), .f(decimaldecoder_4_dout[14]), .a(decimaldecoder_4_dout[13]),
    .b(decimaldecoder_4_dout[12]), .e(decimaldecoder_4_dout[31]), .d(decimaldecoder_4_dout[30]),
    .c(decimaldecoder_4_dout[29]), .dp(decimaldecoder_4_dout[28]));
  LED led_1 ();  // open: in
  _7_Segment_Display u_7_segment_display_11 (
    .g(decimaldecoder_4_dout[11]), .f(decimaldecoder_4_dout[10]), .a(decimaldecoder_4_dout[9]),
    .b(decimaldecoder_4_dout[8]), .e(decimaldecoder_4_dout[27]), .d(decimaldecoder_4_dout[26]),
    .c(decimaldecoder_4_dout[25]), .dp(decimaldecoder_4_dout[24]));
  _7_Segment_Display u_7_segment_display_12 (
    .g(decimaldecoder_4_dout[7]), .f(decimaldecoder_4_dout[6]), .a(decimaldecoder_4_dout[5]),
    .b(decimaldecoder_4_dout[4]), .e(decimaldecoder_4_dout[23]), .d(decimaldecoder_4_dout[22]),
    .c(decimaldecoder_4_dout[21]), .dp(decimaldecoder_4_dout[20]));
  LED led_2 ();  // open: in
  LED led_3 ();  // open: in
  _7_Segment_Display u_7_segment_display_13 (
    .g(decimaldecoder_4_dout[3]), .f(decimaldecoder_4_dout[2]), .a(decimaldecoder_4_dout[1]),
    .b(decimaldecoder_4_dout[0]), .e(decimaldecoder_4_dout[19]), .d(decimaldecoder_4_dout[18]),
    .c(decimaldecoder_4_dout[17]), .dp(decimaldecoder_4_dout[16]));
  LED led_4 ();  // open: in
  LED led_5 ();  // open: in
  LED led_6 ();  // open: in
  LED led_7 ();  // open: in
  LED led_8 ();  // open: in

  // Notes on the sheet:
  //   D7
  //   D6
  //   D5
  //   D4
  //   D2
  //   D3
  //   D1
  //   DO
endmodule

module DecimalDecoder (
  input  [7:0] Din,
  output [31:0] Dout
);

  ROM #(.dataWidth(32)) rom_1 (
    .addr(Din),
    .data({Dout[31:28], Dout[15:12], Dout[27:24], Dout[11:8], Dout[23:20], Dout[7:4], Dout[19:16], Dout[3:0]}));

  // Notes on the sheet:
  //   contents of rom_1 (hex, n*v repeats v):
  //   e7 21 cb 6b 2d 6e ee 23 ef 2f 21e7 2121 21cb 216b 212d 216e 21ee 2123 21ef 212f cbe7 cb21 cbcb cb6b
  //   cb2d cb6e cbee cb23 cbef cb2f 6be7 6b21 6bcb 6b6b 6b2d 6b6e 6bee 6b23 6bef 6b2f 2de7 2d21 2dcb 2d6b
  //   2d2d 2d6e 2dee 2d23 2def 2d2f 6ee7 6e21 6ecb 6e6b 6e2d 6e6e 6eee 6e23 6eef 6e2f eee7 ee21 eecb ee6b
  //   ee2d ee6e eeee ee23 eeef ee2f 23e7 2321 23cb 236b 232d 236e 23ee 2323 23ef 232f efe7 ef21 efcb ef6b
  //   ef2d ef6e efee ef23 efef ef2f 2fe7 2f21 2fcb 2f6b 2f2d 2f6e 2fee 2f23 2fef 2f2f 21e7e7 21e721 21e7cb
  //   21e76b 21e72d 21e76e 21e7ee 21e723 21e7ef 21e72f 2121e7 212121 2121cb 21216b 21212d 21216e 2121ee
  //   212123 2121ef 21212f 21cbe7 21cb21 21cbcb 21cb6b 21cb2d 21cb6e 21cbee 21cb23 21cbef 21cb2f 216be7
  //   216b21 216bcb 216b6b 216b2d 216b6e 216bee 216b23 216bef 216b2f 212de7 212d21 212dcb 212d6b 212d2d
  //   212d6e 212dee 212d23 212def 212d2f 216ee7 216e21 216ecb 216e6b 216e2d 216e6e 216eee 216e23 216eef
  //   216e2f 21eee7 21ee21 21eecb 21ee6b 21ee2d 21ee6e 21eeee 21ee23 21eeef 21ee2f 2123e7 212321 2123cb
  //   21236b 21232d 21236e 2123ee 212323 2123ef 21232f 21efe7 21ef21 21efcb 21ef6b 21ef2d 21ef6e 21efee
  //   21ef23 21efef 21ef2f 212fe7 212f21 212fcb 212f6b 212f2d 212f6e 212fee 212f23 212fef 212f2f cbe7e7
  //   cbe721 cbe7cb cbe76b cbe72d cbe76e cbe7ee cbe723 cbe7ef cbe72f cb21e7 cb2121 cb21cb cb216b cb212d
  //   cb216e cb21ee cb2123 cb21ef cb212f cbcbe7 cbcb21 cbcbcb cbcb6b cbcb2d cbcb6e cbcbee cbcb23 cbcbef
  //   cbcb2f cb6be7 cb6b21 cb6bcb cb6b6b cb6b2d cb6b6e cb6bee cb6b23 cb6bef cb6b2f cb2de7 cb2d21 cb2dcb
  //   cb2d6b cb2d2d cb2d6e cb2dee cb2d23 cb2def cb2d2f cb6ee7 cb6e21 cb6ecb cb6e6b cb6e2d cb6e6e
endmodule
